# Fritzing sketch SAMCO PCB (saved by Fritzing 0.9.3b)
circuit board: 8.80001cm x 4.99999cm
breadboards: 1

parts:
  J1 = female pin header, 2 pins [form="♀ (female)"]
  J2 = female pin header, 2 pins [form="♀ (female)"]
  J6 = female pin header, 2 pins [form="♀ (female)"]
  J7 = female pin header, 2 pins [form="♀ (female)"]
  13 = female pin header, 2 pins [form="♀ (female)"]
  Part3 = Itsy Bitsy M0 Express
  SCL = female pin header, 2 pins [form="♀ (female)"]
  J8 = female pin header, 2 pins [form="♀ (female)"]
  S1 = Momentary Switch [package=tactile-pth]
  J9 = female pin header, 2 pins [form="♀ (female)"]
  LED1 = LED - 5mm [color="Red (633nm)" package="5 mm [THT]"]  # not connected
  LED2 = LED - 5mm [color="Red (633nm)" package="5 mm [THT]"]  # not connected

nets:
  N1: J1.pin1, Part3.A2
  N2: J1.pin2, J2.pin2, J6.pin2, J7.pin2, 13.pin1, Part3.GND, J8.pin2
  N3: J2.pin1, Part3.D5_5V
  N4: J6.pin1, Part3.A3
  N5: J7.pin1, Part3.A4
  N6: 13.pin2, Part3.A1
  N7: Part3.SCL, SCL.pin1
  N8: Part3.SDA, SCL.pin2
  N9: Part3.A5, J8.pin1
  N10: S1.1, S1.2, J9.pin1
  N11: S1.3, S1.4, J9.pin2

custom parts:
  Itsy Bitsy M0 Express: What's smaller than a Feather but larger than a Trinket? It's an Adafruit ItsyBitsy M0 Express! Small, powerful, with a rockin' ATSAMD21 Cortex M0 processor running at 48 MHz - this microcontroller board is perfect when you want something very compact, but still with a bunch of pins. ItsyBitsy M0 Express is only 1.4" long by 0.7" wide, but has 6 power pins, 23 digital GPIO pins (12 of which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
